// Logisim project core.circ as structural Verilog: 6 circuits, main circuit main
module main (
);

  wire aligned_read_helper_1_misaligned, aligned_write_helper_1_misaligned, clock, getbootvec, memread,
       memwrite, not_1_out, reset;
  wire [1:0] core_1_address, memsz;
  wire [23:0] core_1_address_2;
  wire [29:24] core_1_address_3;
  wire [31:0] aligned_read_helper_1_aligned, aligned_write_helper_1_combined, core_1_dout, rom_1_data;

  Clock clock_1 (.out(clock));
  Button button_1 (.out(reset));
  not not_1 (not_1_out, core_1_address_3[24]);
  ROM #(.addrWidth(24), .dataWidth(32)) rom_1 (.addr(core_1_address_2), .data(rom_1_data), .sel(not_1_out));
  RAM #(.addrWidth(24), .dataWidth(32), .bus("separate")) ram_1 (
    .addr(core_1_address_2), .din(aligned_write_helper_1_combined), .data(rom_1_data), .str(memwrite),
    .sel(core_1_address_3[24]), .clk(clock), .ld(1'b1), .clr(1'b0));
  Aligned_write_helper aligned_write_helper_1 (
    .Current(rom_1_data), .New(core_1_dout), .Size(memsz), .Offset(core_1_address),
    .Misaligned(aligned_write_helper_1_misaligned), .Combined(aligned_write_helper_1_combined));
  Aligned_read_helper aligned_read_helper_1 (
    .Raw(rom_1_data), .Size(memsz), .Offset(core_1_address), .Misaligned(aligned_read_helper_1_misaligned),
    .Aligned(aligned_read_helper_1_aligned));
  // OR_Gate or_1: pin names not known; wires that end beside it: aligned_write_helper_1_misaligned, aligned_read_helper_1_misaligned
  core core_1 (
    .Clock(clock), .Reset(reset), .Getbootvec(getbootvec), .Read(memread), .Write(memwrite), .Memsz(memsz),
    .Address({core_1_address_3, core_1_address_2, core_1_address}), .Dout(core_1_dout),
    .Din(aligned_read_helper_1_aligned));
endmodule

// RV23I
module core (
  input  Clock,
  input  Reset,
  input  [31:0] Din,
  output Getbootvec,
  output Read,
  output Write,
  output [1:0] Memsz,
  output [31:0] Address,
  output [31:0] Dout
);

  wire inc, jmp, or_1_out, pull_resistor_13_node, undriven;
  wire [4:0] pull_resistor_9_node, pull_resistor_10_node, pull_resistor_11_node;
  wire [31:0] adder_1_out, alu_1_q, data, multiplexer_1_out, pc_q, pull_resistor_12_node, regfile_1_dout1,
       regfile_1_dout2;

  Pull_Resistor pull_resistor_1 (.node(Address));
  Pull_Resistor pull_resistor_2 (.node(data));
  Pull_Resistor pull_resistor_3 (.node(Getbootvec));
  Pull_Resistor pull_resistor_4 (.node(Read));
  Pull_Resistor pull_resistor_5 (.node(Write));
  Pull_Resistor pull_resistor_6 (.node(Memsz));
  Transistor #(.\type ("n"), .width(32)) transistor_1 (.in(data), .out(Dout), .gate(Write));
  Transistor #(.\type ("n"), .width(32)) transistor_2 (.in(Din), .out(data), .gate(Read));
  Pull_Resistor pull_resistor_7 (.node(jmp));
  Pull_Resistor pull_resistor_8 (.node(inc));
  Pull_Resistor pull_resistor_9 (.node(pull_resistor_9_node));
  Pull_Resistor pull_resistor_10 (.node(pull_resistor_10_node));
  Pull_Resistor pull_resistor_11 (.node(pull_resistor_11_node));
  Multiplexer #(.width(32)) multiplexer_1 (
    .in0(adder_1_out), .in1(pull_resistor_12_node), .out(multiplexer_1_out), .sel(jmp), .en(undriven));
  Pull_Resistor pull_resistor_12 (.node(pull_resistor_12_node));
  regfile regfile_1 (
    .Clock(Clock), .Reset(Reset), .rd(pull_resistor_9_node), .rs1(pull_resistor_10_node),
    .rs2(pull_resistor_11_node), .Dout1(regfile_1_dout1), .Dout2(regfile_1_dout2), .Din(data));  // open: Write
  Register #(.width(32)) pc (.D(multiplexer_1_out), .en(or_1_out), .Q(pc_q), .clk(Clock), .clr(Reset));
  or or_1 (or_1_out, undriven, jmp, inc);
  Adder #(.width(32)) adder_1 (.a(pc_q), .b(32'h4), .out(adder_1_out));  // open: cin, cout
  Pull_Resistor pull_resistor_13 (.node(pull_resistor_13_node));
  ALU alu_1 (
    .Signed_comparison(1'b0), .A(regfile_1_dout1), .B(regfile_1_dout2), .Q(alu_1_q));  // open: A_B, A_B_2, A_B_3
  assign data = pull_resistor_13_node ? alu_1_q : 32'bz;  // Controlled_Buffer controlled_buffer_1

  // Other names for the same wires on the sheet: addr[31:0] = Address; memread = Read; memwrite = Write
endmodule

module regfile (
  input  Clock,
  input  Reset,
  input  [31:0] Din,
  input  Write,
  input  [4:0] rd,
  input  [4:0] rs1,
  input  [4:0] rs2,
  output [31:0] Dout1,
  output [31:0] Dout2
);

  wire and_1_p2, and_2_p2, and_3_p2, and_4_p2, and_5_p2, and_6_p2, and_7_p2, and_8_p2, and_8_p4, and_9_out,
       and_10_out, and_11_p2, and_11_p4, and_12_out, and_13_p2, and_13_p4, and_14_p2, and_14_p4, and_15_out,
       and_16_out, and_17_p2, and_17_p4, and_18_p2, and_18_p4, and_19_out, and_20_out, and_21_p2, and_21_p4,
       and_22_out, and_23_p2, and_23_p4, and_24_p2, and_25_p2, and_26_p2, and_27_p2, and_28_p2, and_29_p2,
       and_30_p2, and_31_p2, and_32_p2, and_32_p4, and_33_p2, and_33_p4, and_34_p2, and_34_p4, and_35_p2,
       and_35_p4, and_36_p2, and_36_p4, and_37_p2, and_37_p4, and_38_p2, and_38_p4, and_39_p2, and_39_p4,
       and_40_out, and_41_p2, and_42_p2, and_43_out, and_44_p2, and_45_out, and_46_p2, and_47_out,
       and_48_out, and_49_p2, and_50_p2, and_51_out, and_52_p2, and_53_out, and_54_out, and_55_p2, and_56_p2,
       and_56_p4, and_57_p2, and_57_p4, and_58_p2, and_58_p4, and_59_p2, and_59_p4, and_60_p2, and_60_p4,
       and_61_p2, and_61_p4, and_62_p2, and_62_p4, and_63_p2, and_63_p4, and_64_p2, and_65_out, and_66_p2,
       and_67_out, and_68_out, and_69_p2, and_70_out, and_71_p2, and_72_out, and_73_p2, and_74_out,
       and_75_p2, and_76_p2, and_77_out, and_78_p2, and_79_out, and_80_p2, and_80_p4, and_81_p2, and_81_p4,
       and_82_p2, and_82_p4, and_83_p2, and_83_p4, and_84_p2, and_84_p4, and_85_p2, and_85_p4, and_86_p2,
       and_86_p4, and_87_p2, and_87_p4, and_88_out, and_89_out, and_90_out, and_91_out, and_92_out,
       and_93_out, and_94_out, and_95_out, decoder_1_out0, decoder_1_out1, decoder_1_out2, decoder_1_out3,
       decoder_1_out4, decoder_1_out5, decoder_1_out6, decoder_1_out7, decoder_2_out0, decoder_2_out1,
       decoder_2_out2, decoder_2_out3, decoder_2_out4, decoder_2_out5, decoder_2_out6, decoder_2_out7,
       decoder_3_out0, decoder_3_out1, decoder_3_out2, decoder_3_out3, decoder_3_out4, decoder_3_out5,
       decoder_3_out6, decoder_3_out7, decoder_4_out0, decoder_4_out1, decoder_4_out2, decoder_4_out3,
       decoder_5_out0, decoder_5_out1, decoder_5_out2, decoder_5_out3, decoder_6_out0, decoder_6_out1,
       decoder_6_out2, decoder_6_out3;
  wire [31:0] x1_q, x2_q, x3_q, x4_q, x5_q, x6_q, x7_q, x8_q, x9_q, x10_q, x11_q, x12_q, x13_q, x15_2_q,
       x15_q, x16_q, x17_q, x18_q, x19_q, x20_q, x21_q, x22_q, x23_q, x24_q, x25_q, x26_q, x27_q, x28_q,
       x29_q, x30_q, x31_q;

  Decoder #(.select(3), .disabled(0)) decoder_1 (
    .out0(decoder_1_out0), .out1(decoder_1_out1), .out2(decoder_1_out2), .out3(decoder_1_out3),
    .out4(decoder_1_out4), .out5(decoder_1_out5), .out6(decoder_1_out6), .out7(decoder_1_out7), .sel(rs2[4:2]));
  Decoder #(.select(3), .disabled(0)) decoder_2 (
    .out0(decoder_2_out0), .out1(decoder_2_out1), .out2(decoder_2_out2), .out3(decoder_2_out3),
    .out4(decoder_2_out4), .out5(decoder_2_out5), .out6(decoder_2_out6), .out7(decoder_2_out7), .sel(rs1[4:2]));
  Decoder #(.select(3), .disabled(0)) decoder_3 (
    .out0(decoder_3_out0), .out1(decoder_3_out1), .out2(decoder_3_out2), .out3(decoder_3_out3),
    .out4(decoder_3_out4), .out5(decoder_3_out5), .out6(decoder_3_out6), .out7(decoder_3_out7), .sel(rd[4:2]));
  Decoder #(.select(2), .disabled(0), .enable("true")) decoder_4 (
    .out0(decoder_4_out0), .out1(decoder_4_out1), .out2(decoder_4_out2), .out3(decoder_4_out3),
    .sel(rd[1:0]), .en(Write));
  Decoder #(.select(2), .disabled(0)) decoder_5 (
    .out0(decoder_5_out0), .out1(decoder_5_out1), .out2(decoder_5_out2), .out3(decoder_5_out3), .sel(rs1[1:0]));  // open: en
  Decoder #(.select(2), .disabled(0)) decoder_6 (
    .out0(decoder_6_out0), .out1(decoder_6_out1), .out2(decoder_6_out2), .out3(decoder_6_out3), .sel(rs2[1:0]));  // open: en
  // AND_Gate and_1: pin names not known; wires that end beside it: decoder_4_out0, and_1_p2, decoder_3_out1
  // AND_Gate and_2: pin names not known; wires that end beside it: decoder_4_out0, and_2_p2, decoder_3_out2
  // AND_Gate and_3: pin names not known; wires that end beside it: decoder_4_out0, and_3_p2, decoder_3_out3
  // AND_Gate and_4: pin names not known; wires that end beside it: decoder_4_out0, and_4_p2, decoder_3_out4
  // AND_Gate and_5: pin names not known; wires that end beside it: decoder_4_out0, and_5_p2, decoder_3_out5
  // AND_Gate and_6: pin names not known; wires that end beside it: decoder_4_out0, and_6_p2, decoder_3_out6
  // AND_Gate and_7: pin names not known; wires that end beside it: decoder_4_out0, and_7_p2, decoder_3_out7
  assign Dout2 = and_9_out ? {32{1'b0}} : 32'bz;  // Controlled_Buffer controlled_buffer_1
  assign Dout1 = and_8_p2 ? {32{1'b0}} : 32'bz;  // Controlled_Buffer controlled_buffer_2
  // AND_Gate and_8: pin names not known; wires that end beside it: decoder_5_out0, and_8_p2, decoder_2_out0, and_8_p4
  and and_9 (and_9_out, and_8_p4, decoder_6_out0, decoder_1_out0);
  assign Dout1 = and_11_p2 ? x4_q : 32'bz;  // Controlled_Buffer controlled_buffer_3
  assign Dout2 = and_10_out ? x4_q : 32'bz;  // Controlled_Buffer controlled_buffer_4
  Register #(.width(32)) x4 (.D(Din), .en(and_1_p2), .Q(x4_q), .clk(Clock), .clr(Reset));
  and and_10 (and_10_out, and_11_p4, decoder_6_out0, decoder_1_out1);
  // AND_Gate and_11: pin names not known; wires that end beside it: decoder_5_out0, and_11_p2, decoder_2_out1, and_11_p4
  assign Dout1 = and_13_p2 ? x8_q : 32'bz;  // Controlled_Buffer controlled_buffer_5
  assign Dout2 = and_12_out ? x8_q : 32'bz;  // Controlled_Buffer controlled_buffer_6
  Register #(.width(32)) x8 (.D(Din), .en(and_2_p2), .Q(x8_q), .clk(Clock), .clr(Reset));
  and and_12 (and_12_out, and_13_p4, decoder_6_out0, decoder_1_out2);
  // AND_Gate and_13: pin names not known; wires that end beside it: decoder_5_out0, and_13_p2, decoder_2_out2, and_13_p4
  assign Dout1 = and_14_p2 ? x12_q : 32'bz;  // Controlled_Buffer controlled_buffer_7
  assign Dout2 = and_15_out ? x12_q : 32'bz;  // Controlled_Buffer controlled_buffer_8
  Register #(.width(32)) x12 (.D(Din), .en(and_3_p2), .Q(x12_q), .clk(Clock), .clr(Reset));
  // AND_Gate and_14: pin names not known; wires that end beside it: decoder_5_out0, and_14_p2, decoder_2_out3, and_14_p4
  and and_15 (and_15_out, and_14_p4, decoder_6_out0, decoder_1_out3);
  assign Dout1 = and_17_p2 ? x16_q : 32'bz;  // Controlled_Buffer controlled_buffer_9
  assign Dout2 = and_16_out ? x16_q : 32'bz;  // Controlled_Buffer controlled_buffer_10
  Register #(.width(32)) x16 (.D(Din), .en(and_4_p2), .Q(x16_q), .clk(Clock), .clr(Reset));
  and and_16 (and_16_out, and_17_p4, decoder_6_out0, decoder_1_out4);
  // AND_Gate and_17: pin names not known; wires that end beside it: decoder_5_out0, and_17_p2, decoder_2_out4, and_17_p4
  assign Dout2 = and_19_out ? x20_q : 32'bz;  // Controlled_Buffer controlled_buffer_11
  assign Dout1 = and_18_p2 ? x20_q : 32'bz;  // Controlled_Buffer controlled_buffer_12
  Register #(.width(32)) x20 (.D(Din), .en(and_5_p2), .Q(x20_q), .clk(Clock), .clr(Reset));
  // AND_Gate and_18: pin names not known; wires that end beside it: decoder_5_out0, and_18_p2, decoder_2_out5, and_18_p4
  and and_19 (and_19_out, and_18_p4, decoder_6_out0, decoder_1_out5);
  assign Dout2 = and_20_out ? x24_q : 32'bz;  // Controlled_Buffer controlled_buffer_13
  assign Dout1 = and_21_p2 ? x24_q : 32'bz;  // Controlled_Buffer controlled_buffer_14
  Register #(.width(32)) x24 (.D(Din), .en(and_6_p2), .Q(x24_q), .clk(Clock), .clr(Reset));
  and and_20 (and_20_out, and_21_p4, decoder_6_out0, decoder_1_out6);
  // AND_Gate and_21: pin names not known; wires that end beside it: decoder_5_out0, and_21_p2, decoder_2_out6, and_21_p4
  assign Dout2 = and_22_out ? x28_q : 32'bz;  // Controlled_Buffer controlled_buffer_15
  assign Dout1 = and_23_p2 ? x28_q : 32'bz;  // Controlled_Buffer controlled_buffer_16
  Register #(.width(32)) x28 (.D(Din), .en(and_7_p2), .Q(x28_q), .clk(Clock), .clr(Reset));
  and and_22 (and_22_out, and_23_p4, decoder_6_out0, decoder_1_out7);
  // AND_Gate and_23: pin names not known; wires that end beside it: decoder_5_out0, and_23_p2, decoder_2_out7, and_23_p4
  // AND_Gate and_24: pin names not known; wires that end beside it: decoder_4_out1, and_24_p2, decoder_3_out0
  // AND_Gate and_25: pin names not known; wires that end beside it: decoder_4_out1, and_25_p2, decoder_3_out1
  // AND_Gate and_26: pin names not known; wires that end beside it: decoder_4_out1, and_26_p2, decoder_3_out2
  // AND_Gate and_27: pin names not known; wires that end beside it: decoder_4_out1, and_27_p2, decoder_3_out3
  // AND_Gate and_28: pin names not known; wires that end beside it: decoder_4_out1, and_28_p2, decoder_3_out4
  // AND_Gate and_29: pin names not known; wires that end beside it: decoder_4_out1, and_29_p2, decoder_3_out5
  // AND_Gate and_30: pin names not known; wires that end beside it: decoder_4_out1, and_30_p2, decoder_3_out6
  // AND_Gate and_31: pin names not known; wires that end beside it: decoder_4_out1, and_31_p2, decoder_3_out7
  assign Dout2 = and_40_out ? x1_q : 32'bz;  // Controlled_Buffer controlled_buffer_17
  assign Dout1 = and_32_p2 ? x1_q : 32'bz;  // Controlled_Buffer controlled_buffer_18
  Register #(.width(32)) x1 (.D(Din), .en(and_24_p2), .Q(x1_q), .clk(Clock), .clr(Reset));
  // AND_Gate and_32: pin names not known; wires that end beside it: decoder_5_out1, and_32_p2, decoder_2_out0, and_32_p4
  assign Dout1 = and_33_p2 ? x5_q : 32'bz;  // Controlled_Buffer controlled_buffer_19
  assign Dout2 = and_43_out ? x5_q : 32'bz;  // Controlled_Buffer controlled_buffer_20
  Register #(.width(32)) x5 (.D(Din), .en(and_25_p2), .Q(x5_q), .clk(Clock), .clr(Reset));
  // AND_Gate and_33: pin names not known; wires that end beside it: decoder_5_out1, and_33_p2, decoder_2_out1, and_33_p4
  assign Dout1 = and_34_p2 ? x9_q : 32'bz;  // Controlled_Buffer controlled_buffer_21
  assign Dout2 = and_45_out ? x9_q : 32'bz;  // Controlled_Buffer controlled_buffer_22
  Register #(.width(32)) x9 (.D(Din), .en(and_26_p2), .Q(x9_q), .clk(Clock), .clr(Reset));
  // AND_Gate and_34: pin names not known; wires that end beside it: decoder_5_out1, and_34_p2, decoder_2_out2, and_34_p4
  assign Dout1 = and_35_p2 ? x13_q : 32'bz;  // Controlled_Buffer controlled_buffer_23
  assign Dout2 = and_47_out ? x13_q : 32'bz;  // Controlled_Buffer controlled_buffer_24
  Register #(.width(32)) x13 (.D(Din), .en(and_27_p2), .Q(x13_q), .clk(Clock), .clr(Reset));
  // AND_Gate and_35: pin names not known; wires that end beside it: decoder_5_out1, and_35_p2, decoder_2_out3, and_35_p4
  assign Dout1 = and_36_p2 ? x17_q : 32'bz;  // Controlled_Buffer controlled_buffer_25
  assign Dout2 = and_48_out ? x17_q : 32'bz;  // Controlled_Buffer controlled_buffer_26
  Register #(.width(32)) x17 (.D(Din), .en(and_28_p2), .Q(x17_q), .clk(Clock), .clr(Reset));
  // AND_Gate and_36: pin names not known; wires that end beside it: decoder_5_out1, and_36_p2, decoder_2_out4, and_36_p4
  assign Dout2 = and_51_out ? x21_q : 32'bz;  // Controlled_Buffer controlled_buffer_27
  assign Dout1 = and_37_p2 ? x21_q : 32'bz;  // Controlled_Buffer controlled_buffer_28
  Register #(.width(32)) x21 (.D(Din), .en(and_29_p2), .Q(x21_q), .clk(Clock), .clr(Reset));
  // AND_Gate and_37: pin names not known; wires that end beside it: decoder_5_out1, and_37_p2, decoder_2_out5, and_37_p4
  assign Dout1 = and_38_p2 ? x25_q : 32'bz;  // Controlled_Buffer controlled_buffer_29
  assign Dout2 = and_53_out ? x25_q : 32'bz;  // Controlled_Buffer controlled_buffer_30
  Register #(.width(32)) x25 (.D(Din), .en(and_30_p2), .Q(x25_q), .clk(Clock), .clr(Reset));
  // AND_Gate and_38: pin names not known; wires that end beside it: decoder_5_out1, and_38_p2, decoder_2_out6, and_38_p4
  assign Dout2 = and_54_out ? x29_q : 32'bz;  // Controlled_Buffer controlled_buffer_31
  assign Dout1 = and_39_p2 ? x29_q : 32'bz;  // Controlled_Buffer controlled_buffer_32
  Register #(.width(32)) x29 (.D(Din), .en(and_31_p2), .Q(x29_q), .clk(Clock), .clr(Reset));
  // AND_Gate and_39: pin names not known; wires that end beside it: decoder_5_out1, and_39_p2, decoder_2_out7, and_39_p4
  and and_40 (and_40_out, and_32_p4, decoder_6_out1, decoder_1_out0);
  // AND_Gate and_41: pin names not known; wires that end beside it: decoder_4_out2, and_41_p2, decoder_3_out0
  // AND_Gate and_42: pin names not known; wires that end beside it: decoder_4_out2, and_42_p2, decoder_3_out1
  and and_43 (and_43_out, and_33_p4, decoder_6_out1, decoder_1_out1);
  // AND_Gate and_44: pin names not known; wires that end beside it: decoder_4_out2, and_44_p2, decoder_3_out2
  and and_45 (and_45_out, and_34_p4, decoder_6_out1, decoder_1_out2);
  // AND_Gate and_46: pin names not known; wires that end beside it: decoder_4_out2, and_46_p2, decoder_3_out3
  and and_47 (and_47_out, and_35_p4, decoder_6_out1, decoder_1_out3);
  and and_48 (and_48_out, and_36_p4, decoder_6_out1, decoder_1_out4);
  // AND_Gate and_49: pin names not known; wires that end beside it: decoder_4_out2, and_49_p2, decoder_3_out4
  // AND_Gate and_50: pin names not known; wires that end beside it: decoder_4_out2, and_50_p2, decoder_3_out5
  and and_51 (and_51_out, and_37_p4, decoder_6_out1, decoder_1_out5);
  // AND_Gate and_52: pin names not known; wires that end beside it: decoder_4_out2, and_52_p2, decoder_3_out6
  and and_53 (and_53_out, and_38_p4, decoder_6_out1, decoder_1_out6);
  and and_54 (and_54_out, and_39_p4, decoder_6_out1, decoder_1_out7);
  // AND_Gate and_55: pin names not known; wires that end beside it: decoder_4_out2, and_55_p2, decoder_3_out7
  assign Dout1 = and_56_p2 ? x2_q : 32'bz;  // Controlled_Buffer controlled_buffer_33
  Register #(.width(32)) x2 (.D(Din), .en(and_41_p2), .Q(x2_q), .clk(Clock), .clr(Reset));
  // AND_Gate and_56: pin names not known; wires that end beside it: decoder_5_out2, and_56_p2, decoder_2_out0, and_56_p4
  assign Dout1 = and_57_p2 ? x6_q : 32'bz;  // Controlled_Buffer controlled_buffer_34
  Register #(.width(32)) x6 (.D(Din), .en(and_42_p2), .Q(x6_q), .clk(Clock), .clr(Reset));
  // AND_Gate and_57: pin names not known; wires that end beside it: decoder_5_out2, and_57_p2, decoder_2_out1, and_57_p4
  assign Dout1 = and_58_p2 ? x10_q : 32'bz;  // Controlled_Buffer controlled_buffer_35
  Register #(.width(32)) x10 (.D(Din), .en(and_44_p2), .Q(x10_q), .clk(Clock), .clr(Reset));
  // AND_Gate and_58: pin names not known; wires that end beside it: decoder_5_out2, and_58_p2, decoder_2_out2, and_58_p4
  assign Dout1 = and_59_p2 ? x15_q : 32'bz;  // Controlled_Buffer controlled_buffer_36
  Register #(.width(32)) x15 (.D(Din), .en(and_46_p2), .Q(x15_q), .clk(Clock), .clr(Reset));
  // AND_Gate and_59: pin names not known; wires that end beside it: decoder_5_out2, and_59_p2, decoder_2_out3, and_59_p4
  assign Dout1 = and_60_p2 ? x18_q : 32'bz;  // Controlled_Buffer controlled_buffer_37
  Register #(.width(32)) x18 (.D(Din), .en(and_49_p2), .Q(x18_q), .clk(Clock), .clr(Reset));
  // AND_Gate and_60: pin names not known; wires that end beside it: decoder_5_out2, and_60_p2, decoder_2_out4, and_60_p4
  assign Dout1 = and_61_p2 ? x22_q : 32'bz;  // Controlled_Buffer controlled_buffer_38
  Register #(.width(32)) x22 (.D(Din), .en(and_50_p2), .Q(x22_q), .clk(Clock), .clr(Reset));
  // AND_Gate and_61: pin names not known; wires that end beside it: decoder_5_out2, and_61_p2, decoder_2_out5, and_61_p4
  assign Dout1 = and_62_p2 ? x26_q : 32'bz;  // Controlled_Buffer controlled_buffer_39
  Register #(.width(32)) x26 (.D(Din), .en(and_52_p2), .Q(x26_q), .clk(Clock), .clr(Reset));
  // AND_Gate and_62: pin names not known; wires that end beside it: decoder_5_out2, and_62_p2, decoder_2_out6, and_62_p4
  assign Dout1 = and_63_p2 ? x30_q : 32'bz;  // Controlled_Buffer controlled_buffer_40
  Register #(.width(32)) x30 (.D(Din), .en(and_55_p2), .Q(x30_q), .clk(Clock), .clr(Reset));
  // AND_Gate and_63: pin names not known; wires that end beside it: decoder_5_out2, and_63_p2, decoder_2_out7, and_63_p4
  assign Dout2 = and_65_out ? x2_q : 32'bz;  // Controlled_Buffer controlled_buffer_41
  // AND_Gate and_64: pin names not known; wires that end beside it: decoder_4_out3, and_64_p2, decoder_3_out0
  and and_65 (and_65_out, and_56_p4, decoder_6_out2, decoder_1_out0);
  assign Dout2 = and_67_out ? x6_q : 32'bz;  // Controlled_Buffer controlled_buffer_42
  // AND_Gate and_66: pin names not known; wires that end beside it: decoder_4_out3, and_66_p2, decoder_3_out1
  and and_67 (and_67_out, and_57_p4, decoder_6_out2, decoder_1_out1);
  assign Dout2 = and_68_out ? x10_q : 32'bz;  // Controlled_Buffer controlled_buffer_43
  and and_68 (and_68_out, and_58_p4, decoder_6_out2, decoder_1_out2);
  // AND_Gate and_69: pin names not known; wires that end beside it: decoder_4_out3, and_69_p2, decoder_3_out2
  assign Dout2 = and_70_out ? x15_q : 32'bz;  // Controlled_Buffer controlled_buffer_44
  and and_70 (and_70_out, and_59_p4, decoder_6_out2, decoder_1_out3);
  // AND_Gate and_71: pin names not known; wires that end beside it: decoder_4_out3, and_71_p2, decoder_3_out3
  assign Dout2 = and_72_out ? x18_q : 32'bz;  // Controlled_Buffer controlled_buffer_45
  and and_72 (and_72_out, and_60_p4, decoder_6_out2, decoder_1_out4);
  // AND_Gate and_73: pin names not known; wires that end beside it: decoder_4_out3, and_73_p2, decoder_3_out4
  assign Dout2 = and_74_out ? x22_q : 32'bz;  // Controlled_Buffer controlled_buffer_46
  and and_74 (and_74_out, and_61_p4, decoder_6_out2, decoder_1_out5);
  // AND_Gate and_75: pin names not known; wires that end beside it: decoder_4_out3, and_75_p2, decoder_3_out5
  assign Dout2 = and_77_out ? x26_q : 32'bz;  // Controlled_Buffer controlled_buffer_47
  // AND_Gate and_76: pin names not known; wires that end beside it: decoder_4_out3, and_76_p2, decoder_3_out6
  and and_77 (and_77_out, and_62_p4, decoder_6_out2, decoder_1_out6);
  assign Dout2 = and_79_out ? x30_q : 32'bz;  // Controlled_Buffer controlled_buffer_48
  // AND_Gate and_78: pin names not known; wires that end beside it: decoder_4_out3, and_78_p2, decoder_3_out7
  and and_79 (and_79_out, and_63_p4, decoder_6_out2, decoder_1_out7);
  assign Dout1 = and_80_p2 ? x3_q : 32'bz;  // Controlled_Buffer controlled_buffer_49
  Register #(.width(32)) x3 (.D(Din), .en(and_64_p2), .Q(x3_q), .clk(Clock), .clr(Reset));
  // AND_Gate and_80: pin names not known; wires that end beside it: decoder_5_out3, and_80_p2, decoder_2_out0, and_80_p4
  assign Dout1 = and_81_p2 ? x7_q : 32'bz;  // Controlled_Buffer controlled_buffer_50
  Register #(.width(32)) x7 (.D(Din), .en(and_66_p2), .Q(x7_q), .clk(Clock), .clr(Reset));
  // AND_Gate and_81: pin names not known; wires that end beside it: decoder_5_out3, and_81_p2, decoder_2_out1, and_81_p4
  assign Dout1 = and_82_p2 ? x11_q : 32'bz;  // Controlled_Buffer controlled_buffer_51
  Register #(.width(32)) x11 (.D(Din), .en(and_69_p2), .Q(x11_q), .clk(Clock), .clr(Reset));
  // AND_Gate and_82: pin names not known; wires that end beside it: decoder_5_out3, and_82_p2, decoder_2_out2, and_82_p4
  assign Dout1 = and_83_p2 ? x15_2_q : 32'bz;  // Controlled_Buffer controlled_buffer_52
  Register #(.width(32)) x15_2 (.D(Din), .en(and_71_p2), .Q(x15_2_q), .clk(Clock), .clr(Reset));
  // AND_Gate and_83: pin names not known; wires that end beside it: decoder_5_out3, and_83_p2, decoder_2_out3, and_83_p4
  assign Dout1 = and_84_p2 ? x19_q : 32'bz;  // Controlled_Buffer controlled_buffer_53
  Register #(.width(32)) x19 (.D(Din), .en(and_73_p2), .Q(x19_q), .clk(Clock), .clr(Reset));
  // AND_Gate and_84: pin names not known; wires that end beside it: decoder_5_out3, and_84_p2, decoder_2_out4, and_84_p4
  assign Dout1 = and_85_p2 ? x23_q : 32'bz;  // Controlled_Buffer controlled_buffer_54
  Register #(.width(32)) x23 (.D(Din), .en(and_75_p2), .Q(x23_q), .clk(Clock), .clr(Reset));
  // AND_Gate and_85: pin names not known; wires that end beside it: decoder_5_out3, and_85_p2, decoder_2_out5, and_85_p4
  assign Dout1 = and_86_p2 ? x27_q : 32'bz;  // Controlled_Buffer controlled_buffer_55
  Register #(.width(32)) x27 (.D(Din), .en(and_76_p2), .Q(x27_q), .clk(Clock), .clr(Reset));
  // AND_Gate and_86: pin names not known; wires that end beside it: decoder_5_out3, and_86_p2, decoder_2_out6, and_86_p4
  assign Dout1 = and_87_p2 ? x31_q : 32'bz;  // Controlled_Buffer controlled_buffer_56
  Register #(.width(32)) x31 (.D(Din), .en(and_78_p2), .Q(x31_q), .clk(Clock), .clr(Reset));
  // AND_Gate and_87: pin names not known; wires that end beside it: decoder_5_out3, and_87_p2, decoder_2_out7, and_87_p4
  assign Dout2 = and_88_out ? x3_q : 32'bz;  // Controlled_Buffer controlled_buffer_57
  and and_88 (and_88_out, and_80_p4, decoder_6_out3, decoder_1_out0);
  assign Dout2 = and_89_out ? x7_q : 32'bz;  // Controlled_Buffer controlled_buffer_58
  and and_89 (and_89_out, and_81_p4, decoder_6_out3, decoder_1_out1);
  assign Dout2 = and_90_out ? x11_q : 32'bz;  // Controlled_Buffer controlled_buffer_59
  and and_90 (and_90_out, and_82_p4, decoder_6_out3, decoder_1_out2);
  assign Dout2 = and_91_out ? x15_2_q : 32'bz;  // Controlled_Buffer controlled_buffer_60
  and and_91 (and_91_out, and_83_p4, decoder_6_out3, decoder_1_out3);
  assign Dout2 = and_92_out ? x19_q : 32'bz;  // Controlled_Buffer controlled_buffer_61
  and and_92 (and_92_out, and_84_p4, decoder_6_out3, decoder_1_out4);
  assign Dout2 = and_93_out ? x23_q : 32'bz;  // Controlled_Buffer controlled_buffer_62
  and and_93 (and_93_out, and_85_p4, decoder_6_out3, decoder_1_out5);
  assign Dout2 = and_94_out ? x27_q : 32'bz;  // Controlled_Buffer controlled_buffer_63
  and and_94 (and_94_out, and_86_p4, decoder_6_out3, decoder_1_out6);
  assign Dout2 = and_95_out ? x31_q : 32'bz;  // Controlled_Buffer controlled_buffer_64
  and and_95 (and_95_out, and_87_p4, decoder_6_out3, decoder_1_out7);
endmodule

module ALU (
  input  Signed_comparison,
  input  [31:0] A,
  input  [31:0] B,
  output A_B,
  output A_B_2,
  output A_B_3,
  output [31:0] Q
);

  wire comparator_1_eq, comparator_1_gt, comparator_1_lt, comparator_2_eq, comparator_2_gt, comparator_2_lt,
       not_1_out, pull_resistor_1_node;
  wire [4:0] bit_extender_1_out;
  wire [31:0] adder_1_out, and_1_out, or_1_out, shifter_1_out, shifter_2_out, shifter_3_out,
       subtractor_1_out, undriven, undriven_2, xor_1_out;

  Bit_Extender #(.in_width(32), .out_width(5)) bit_extender_1 (.in(B), .out(bit_extender_1_out));
  assign A_B = Signed_comparison ? comparator_1_gt : 1'bz;  // Controlled_Buffer controlled_buffer_1
  assign A_B_2 = Signed_comparison ? comparator_1_eq : 1'bz;  // Controlled_Buffer controlled_buffer_2
  Comparator #(.width(32)) comparator_1 (
    .a(A), .b(B), .gt(comparator_1_gt), .eq(comparator_1_eq), .lt(comparator_1_lt));
  assign A_B_3 = Signed_comparison ? comparator_1_lt : 1'bz;  // Controlled_Buffer controlled_buffer_3
  assign A_B = not_1_out ? comparator_2_gt : 1'bz;  // Controlled_Buffer controlled_buffer_4
  Comparator #(.width(32), .mode("unsigned")) comparator_2 (
    .a(A), .b(B), .gt(comparator_2_gt), .eq(comparator_2_eq), .lt(comparator_2_lt));
  assign A_B_2 = not_1_out ? comparator_2_eq : 1'bz;  // Controlled_Buffer controlled_buffer_5
  assign A_B_3 = not_1_out ? comparator_2_lt : 1'bz;  // Controlled_Buffer controlled_buffer_6
  Adder #(.width(32)) adder_1 (.a(A), .b(B), .out(adder_1_out));  // open: cin, cout
  Subtractor #(.width(32)) subtractor_1 (.a(A), .b(B), .out(subtractor_1_out));  // open: bin, bout
  assign and_1_out = A & B & undriven;  // AND_Gate and_1, 32 bits wide
  assign or_1_out = undriven | A | B | undriven_2;  // OR_Gate or_1, 32 bits wide
  ExactlyOne xor_1[31:0] (.out(xor_1_out), .in0(undriven_2), .in1(A), .in3(B));
  Shifter #(.width(32)) shifter_1 (.in(A), .\dist (bit_extender_1_out), .out(shifter_1_out));
  Shifter #(.width(32), .shift("lr")) shifter_2 (.in(A), .\dist (bit_extender_1_out), .out(shifter_2_out));
  Shifter #(.width(32), .shift("ar")) shifter_3 (.in(A), .\dist (bit_extender_1_out), .out(shifter_3_out));
  not not_1 (not_1_out, Signed_comparison);
  assign Q = pull_resistor_1_node ? adder_1_out : 32'bz;  // Controlled_Buffer controlled_buffer_7
  assign Q = pull_resistor_1_node ? subtractor_1_out : 32'bz;  // Controlled_Buffer controlled_buffer_8
  assign Q = pull_resistor_1_node ? and_1_out : 32'bz;  // Controlled_Buffer controlled_buffer_9
  assign Q = pull_resistor_1_node ? or_1_out : 32'bz;  // Controlled_Buffer controlled_buffer_10
  assign Q = pull_resistor_1_node ? xor_1_out : 32'bz;  // Controlled_Buffer controlled_buffer_11
  assign Q = pull_resistor_1_node ? shifter_1_out : 32'bz;  // Controlled_Buffer controlled_buffer_12
  assign Q = pull_resistor_1_node ? shifter_2_out : 32'bz;  // Controlled_Buffer controlled_buffer_13
  assign Q = pull_resistor_1_node ? shifter_3_out : 32'bz;  // Controlled_Buffer controlled_buffer_14
  Pull_Resistor pull_resistor_1 (.node(pull_resistor_1_node));
endmodule

module Aligned_write_helper (
  input  [31:0] Current,
  input  [31:0] New,
  input  [1:0] Size,
  input  [1:0] Offset,
  output Misaligned,
  output [31:0] Combined
);

  wire decoder_1_out0, decoder_1_out1, decoder_1_out2, decoder_1_out3, or_1_out, or_2_out;
  wire [7:0] multiplexer_4_out, multiplexer_5_out, multiplexer_6_out, multiplexer_7_out;
  wire [15:0] multiplexer_2_out, multiplexer_3_out;
  wire [31:0] multiplexer_1_out;

  Multiplexer #(.width(32)) multiplexer_1 (.in0(Current), .in1(New), .out(multiplexer_1_out), .sel(decoder_1_out0));
  Multiplexer #(.width(16)) multiplexer_2 (
    .in0(Current[15:0]), .in1(New[15:0]), .out(multiplexer_2_out), .sel(decoder_1_out0));
  Multiplexer #(.width(16)) multiplexer_3 (
    .in0(Current[31:16]), .in1(New[15:0]), .out(multiplexer_3_out), .sel(decoder_1_out2));
  Multiplexer #(.width(8)) multiplexer_4 (
    .in0(Current[7:0]), .in1(New[7:0]), .out(multiplexer_4_out), .sel(decoder_1_out0));
  Multiplexer #(.width(8)) multiplexer_5 (
    .in0(Current[15:8]), .in1(New[7:0]), .out(multiplexer_5_out), .sel(decoder_1_out1));
  Multiplexer #(.width(8)) multiplexer_6 (
    .in0(Current[23:16]), .in1(New[7:0]), .out(multiplexer_6_out), .sel(decoder_1_out2));
  Multiplexer #(.width(8)) multiplexer_7 (
    .in0(Current[31:24]), .in1(New[7:0]), .out(multiplexer_7_out), .sel(decoder_1_out3));
  Decoder #(.select(2)) decoder_1 (
    .out0(decoder_1_out0), .out1(decoder_1_out1), .out2(decoder_1_out2), .out3(decoder_1_out3), .sel(Offset));  // open: en
  or or_1 (or_1_out, decoder_1_out1, decoder_1_out3, decoder_1_out1);
  or or_2 (or_2_out, decoder_1_out1, decoder_1_out2, decoder_1_out3);
  Multiplexer #(.select(2)) multiplexer_8 (
    .in0(1'b0), .in1(or_1_out), .in2(or_2_out), .in3(1'b1), .out(Misaligned), .sel(Size));  // open: en
  Multiplexer #(.select(2), .width(32)) multiplexer_9 (
    .in0({multiplexer_7_out, multiplexer_6_out, multiplexer_5_out, multiplexer_4_out}),
    .in1({multiplexer_3_out, multiplexer_2_out}), .in2(multiplexer_1_out), .in3(Current), .out(Combined),
    .sel(Size));  // open: en
endmodule

module Aligned_read_helper (
  input  [31:0] Raw,
  input  [1:0] Size,
  input  [1:0] Offset,
  output Misaligned,
  output [31:0] Aligned
);

  wire or_1_p3;
  wire [7:0] multiplexer_1_out;
  wire [15:0] multiplexer_2_out;
  wire [31:0] bit_extender_1_out, bit_extender_2_out;

  Multiplexer #(.select(2), .width(8)) multiplexer_1 (
    .in0(Raw[7:0]), .in1(Raw[15:8]), .in2(Raw[23:16]), .in3(Raw[31:24]), .out(multiplexer_1_out), .sel(Offset));  // open: en
  Multiplexer #(.width(16)) multiplexer_2 (
    .in0(Raw[15:0]), .in1(Raw[31:16]), .out(multiplexer_2_out), .sel(Offset[1]));  // open: en
  // OR_Gate or_1: pin names not known; wires that end beside it: Offset[1], Offset[0], or_1_p3
  assign bit_extender_1_out = {{24{1'b0}}, multiplexer_1_out};  // Bit_Extender bit_extender_1
  assign bit_extender_2_out = {{16{1'b0}}, multiplexer_2_out};  // Bit_Extender bit_extender_2
  Multiplexer #(.select(2)) multiplexer_3 (
    .in0(1'b0), .in1(Offset[0]), .in2(or_1_p3), .in3(1'b1), .out(Misaligned), .sel(Size));  // open: en
  Multiplexer #(.select(2), .width(32)) multiplexer_4 (
    .in0(bit_extender_1_out), .in1(bit_extender_2_out), .in2(Raw), .out(Aligned), .sel(Size));  // open: in3, en
endmodule
